// Logisim project ALU.circ as structural Verilog: 3 circuits, main circuit ALU
module ALU (
  input  [31:0] A,
  input  [31:0] B,
  input  [4:0] Shift,
  input  CarryIn,
  input  [3:0] Codop,
  output [31:0] S,
  output [3:0] Flags
);

  wire adder_1_cout, adder_2_cout, adder_3_cout, bitselector_1_out, bitselector_2_out, bitselector_3_out,
       bitselector_4_out, overflow_additionneur_1_overflow, overflow_additionneur_2_overflow,
       overflow_additionneur_3_overflow, overflow_soustracteur_1_overflow, subtractor_3_bout,
       subtractor_4_bout;
  wire [31:0] A_t, adder_1_out, adder_2_out, adder_3_out, ANDD_out, B_t, BIC_out, EOR_out, multiplexer_1_out,
       multiplier_1_out, not_1_out, not_2_out, ORR_out, shifter_1_out, shifter_2_out, shifter_3_out,
       shifter_4_out, subtractor_1_out, subtractor_2_out, subtractor_3_out, subtractor_4_out, TST_out;

  assign ANDD_out = A & B;  // AND_Gate ANDD, 32 bits wide
  assign EOR_out = A ^ B;  // XOR_Gate EOR, 32 bits wide
  Shifter #(.width(32)) shifter_1 (.in(B), .\dist (Shift), .out(shifter_1_out));
  Shifter #(.width(32), .shift("lr")) shifter_2 (.in(B), .\dist (Shift), .out(shifter_2_out));
  Shifter #(.width(32), .shift("ar")) shifter_3 (.in(B), .\dist (Shift), .out(shifter_3_out));
  Adder #(.width(32)) adder_1 (.a(A), .b(B), .out(adder_1_out), .cin(CarryIn), .cout(adder_1_cout));
  Subtractor #(.width(32)) subtractor_1 (.a(A), .b(B), .out(subtractor_1_out));  // open: bin, bout
  Subtractor #(.width(32)) subtractor_2 (
    .a({32{1'b0}}), .b(32'h1), .out(subtractor_2_out), .bin(CarryIn));  // open: bout
  Shifter #(.width(32), .shift("rr")) shifter_4 (.in(B), .\dist (Shift), .out(shifter_4_out));
  assign TST_out = A & B;  // AND_Gate TST, 32 bits wide
  Subtractor #(.width(32)) subtractor_3 (
    .a({32{1'b0}}), .b(B), .out(subtractor_3_out), .bout(subtractor_3_bout));  // open: bin
  Subtractor #(.width(32)) subtractor_4 (.a(A), .b(B), .out(subtractor_4_out), .bout(subtractor_4_bout));  // open: bin
  Adder #(.width(32)) adder_2 (.a(A), .b(B), .out(adder_2_out), .cout(adder_2_cout));  // open: cin
  assign ORR_out = A | B;  // OR_Gate ORR, 32 bits wide
  Multiplier #(.width(32)) multiplier_1 (.a(A), .b(B), .out(multiplier_1_out));  // open: cin, cout
  assign not_1_out = ~B;  // NOT_Gate not_1, 32 bits wide
  assign not_2_out = ~B;  // NOT_Gate not_2, 32 bits wide
  Adder #(.width(32)) adder_3 (
    .a(subtractor_1_out), .b(subtractor_2_out), .out(adder_3_out), .cout(adder_3_cout));  // open: cin
  assign BIC_out = A & not_1_out;  // AND_Gate BIC, 32 bits wide
  Multiplexer #(.select(4), .width(32), .enable("false")) multiplexer_1 (
    .in0(ANDD_out), .in1(EOR_out), .in2(shifter_1_out), .in3(shifter_2_out), .in4(shifter_3_out),
    .in5(adder_1_out), .in6(adder_3_out), .in7(shifter_4_out), .in8(TST_out), .in9(subtractor_3_out),
    .in10(subtractor_4_out), .in11(adder_2_out), .in12(ORR_out), .in13(multiplier_1_out), .in14(BIC_out),
    .in15(not_2_out), .out(multiplexer_1_out), .sel(Codop));
  Comparator #(.width(32)) comparator_1 (.a(multiplexer_1_out), .eq(Flags[1]), .lt(Flags[0]));  // open: b, gt
  Multiplexer #(.select(4), .width(32), .enable("false")) multiplexer_2 (
    .in0(ANDD_out), .in1(EOR_out), .in2(shifter_1_out), .in3(shifter_2_out), .in4(shifter_3_out),
    .in5(adder_1_out), .in6(adder_3_out), .in7(shifter_4_out), .in8(B_t), .in9(subtractor_3_out), .in10(B_t),
    .in11(B_t), .in12(ORR_out), .in13(multiplier_1_out), .in14(BIC_out), .in15(not_2_out), .out(S),
    .sel(Codop));
  BitSelector #(.width(32)) bitselector_1 (.in(shifter_1_out), .out(bitselector_1_out), .sel({5{1'b1}}));
  BitSelector #(.width(32)) bitselector_2 (.in(shifter_2_out), .out(bitselector_2_out), .sel({5{1'b1}}));
  BitSelector #(.width(32)) bitselector_3 (.in(shifter_3_out), .out(bitselector_3_out), .sel({5{1'b1}}));
  BitSelector #(.width(32)) bitselector_4 (.in(shifter_4_out), .out(bitselector_4_out), .sel({5{1'b1}}));
  Multiplexer #(.select(4), .enable("false")) multiplexer_3 (
    .in0(1'b0), .in1(1'b0), .in2(bitselector_1_out), .in3(bitselector_2_out), .in4(bitselector_3_out),
    .in5(adder_1_cout), .in6(adder_3_cout), .in7(bitselector_4_out), .in8(1'b0), .in9(1'b0),
    .in10(subtractor_3_bout), .in11(subtractor_4_bout), .in12(adder_2_cout), .in13(1'b0), .in14(1'b0),
    .in15(1'b0), .out(Flags[2]), .sel(Codop));
  Overflow_Additionneur overflow_additionneur_1 (
    .S(adder_1_out), .A(A_t), .B(B_t), .Overflow(overflow_additionneur_1_overflow));
  Overflow_Additionneur overflow_additionneur_2 (
    .S(adder_3_out), .A(A_t), .B(B_t), .Overflow(overflow_additionneur_2_overflow));
  Overflow_Soustracteur overflow_soustracteur_1 (
    .S(subtractor_4_out), .A(A_t), .B(B_t), .Overflow(overflow_soustracteur_1_overflow));
  Overflow_Additionneur overflow_additionneur_3 (
    .S(adder_2_out), .A(A_t), .B(B_t), .Overflow(overflow_additionneur_3_overflow));
  Multiplexer #(.select(4), .enable("false")) multiplexer_4 (
    .in0(1'b0), .in1(1'b0), .in2(1'b0), .in3(1'b0), .in4(1'b0), .in5(overflow_additionneur_1_overflow),
    .in6(overflow_additionneur_2_overflow), .in7(1'b0), .in8(1'b0), .in9(1'b0),
    .in10(overflow_soustracteur_1_overflow), .in11(overflow_additionneur_3_overflow), .in12(1'b0),
    .in13(1'b0), .in14(1'b0), .in15(1'b0), .out(Flags[3]), .sel(Codop));

  // Other names for the same wires on the sheet: N = Flags[0]; Z = Flags[1]; C = Flags[2]; V = Flags[3]

  // Notes on the sheet:
  //   Note: for ROR, C = N
  //   Note 2: assume that shift > 0 for LSL and LSR
endmodule

module Overflow_Additionneur (
  input  [31:0] S,
  input  [31:0] A,
  input  [31:0] B,
  output Overflow
);

  wire and_1_out, and_2_out, bitselector_1_out, bitselector_2_out, bitselector_3_out;

  BitSelector #(.width(32)) bitselector_1 (.in(S), .out(bitselector_1_out), .sel({5{1'b1}}));
  BitSelector #(.width(32)) bitselector_2 (.in(A), .out(bitselector_2_out), .sel({5{1'b1}}));
  BitSelector #(.width(32)) bitselector_3 (.in(B), .out(bitselector_3_out), .sel({5{1'b1}}));
  and and_1 (and_1_out, ~bitselector_1_out, bitselector_2_out, bitselector_3_out);  // AND_Gate
  and and_2 (and_2_out, bitselector_1_out, ~bitselector_2_out, ~bitselector_3_out);  // AND_Gate
  or or_1 (Overflow, and_1_out, and_2_out);
endmodule

module Overflow_Soustracteur (
  input  [31:0] S,
  input  [31:0] A,
  input  [31:0] B,
  output Overflow
);

  wire and_1_out, and_2_out, bitselector_1_out, bitselector_2_out, bitselector_3_out;

  BitSelector #(.width(32)) bitselector_1 (.in(S), .out(bitselector_1_out), .sel({5{1'b1}}));
  BitSelector #(.width(32)) bitselector_2 (.in(A), .out(bitselector_2_out), .sel({5{1'b1}}));
  BitSelector #(.width(32)) bitselector_3 (.in(B), .out(bitselector_3_out), .sel({5{1'b1}}));
  and and_1 (and_1_out, bitselector_1_out, ~bitselector_2_out, bitselector_3_out);  // AND_Gate
  and and_2 (and_2_out, ~bitselector_1_out, bitselector_2_out, ~bitselector_3_out);  // AND_Gate
  or or_1 (Overflow, and_1_out, and_2_out);
endmodule
