// Logisim project Data_Processing_1.circ as structural Verilog
module Data_Processing (
  input  in_1,
  input  [15:0] in_2,
  output [2:0] out_3,
  output [2:0] out_4,
  output [2:0] out_5,
  output [3:0] out_6,
  output [3:0] out_7
);

  wire [2:0] bit_extender_1_out, bit_extender_2_out, bit_extender_3_out, Rd, Rn;
  wire [3:0] bit_extender_4_out, bit_extender_5_out, multiplexer_3_out;

  Multiplexer #(.select(4), .width(3), .enable("false")) multiplexer_1 (
    .in0(in_2[15:13]), .in1(in_2[15:13]), .in2(in_2[15:13]), .in3(in_2[15:13]), .in4(in_2[15:13]),
    .in5(in_2[15:13]), .in6(in_2[15:13]), .in7(in_2[15:13]), .in8(3'b000), .in9(in_2[15:13]), .in10(3'b000),
    .in11(3'b000), .in12(in_2[15:13]), .in13(in_2[15:13]), .in14(in_2[15:13]), .in15(in_2[15:13]), .out(Rd),
    .sel(in_2[9:6]));
  Multiplexer #(.select(4), .width(3), .enable("false")) multiplexer_2 (
    .in0(in_2[15:13]), .in1(in_2[15:13]), .in2(in_2[15:13]), .in3(in_2[15:13]), .in4(in_2[15:13]),
    .in5(in_2[15:13]), .in6(in_2[15:13]), .in7(in_2[15:13]), .in8(in_2[15:13]), .in9(in_2[15:13]),
    .in10(in_2[15:13]), .in11(in_2[15:13]), .in12(in_2[15:13]), .in13(in_2[15:13]), .in14(in_2[15:13]),
    .in15(3'b000), .out(Rn), .sel(in_2[9:6]));
  assign bit_extender_1_out = {{2{in_1}}, in_1};  // Bit_Extender bit_extender_1
  assign bit_extender_2_out = {{2{in_1}}, in_1};  // Bit_Extender bit_extender_2
  assign bit_extender_3_out = {{2{in_1}}, in_1};  // Bit_Extender bit_extender_3
  assign bit_extender_4_out = {{3{in_1}}, in_1};  // Bit_Extender bit_extender_4
  assign out_3 = Rn & bit_extender_1_out;  // AND_Gate and_1, 3 bits wide
  assign out_4 = Rd & bit_extender_2_out;  // AND_Gate and_2, 3 bits wide
  assign out_5 = in_2[12:10] & bit_extender_3_out;  // AND_Gate and_3, 3 bits wide
  assign out_6 = in_2[9:6] & bit_extender_4_out;  // AND_Gate and_4, 4 bits wide
  assign bit_extender_5_out = {{3{in_1}}, in_1};  // Bit_Extender bit_extender_5
  Multiplexer #(.select(4), .width(4), .enable("false")) multiplexer_3 (
    .in0(4'b1110), .in1(4'b1110), .in2(4'b1110), .in3(4'b1110), .in4(4'b1110), .in5(4'b1111), .in6(4'b1111),
    .in7(4'b1110), .in9(4'b1111), .in10(4'b1111), .in11(4'b1111), .in12(4'b1110), .in13(4'b1100),
    .in14(4'b1110), .in15(4'b1110), .out(multiplexer_3_out), .sel(in_2[9:6]));  // open: in8
  assign out_7 = bit_extender_5_out & multiplexer_3_out;  // AND_Gate and_5, 4 bits wide

  // Other names for the same wires on the sheet: OP[3:0] = in_2[9:6]; Rm[2:0] = in_2[12:10]; Rdn[2:0] = in_2[15:13]

  // Notes on the sheet:
  //   Note 2: RSB instruction has Rn as 1st operand.
  //   MUL instruction has Rn as 1st operand and Rdm as 2nd operand
  //   Pull output low on Enable = 0
  //   For simplification purposes, Rm is used for 1st operand both here and in the ALU.
  //   Note: instructions that does not save the result will still have the second operand as the destination register, the ALU will copy the second register to the destination register
endmodule
