// Logisim project Load_Store_1.circ as structural Verilog
module Load_Store (
  input  [15:0] in_1,
  input  [31:0] in_2,
  input  in_3,
  input  in_4,
  input  in_5,
  output [7:0] out_6,
  output out_7,
  output out_8,
  output [2:0] out_9,
  output [2:0] out_10,
  output [31:0] out_11,
  output out_12
);

  wire and_1_out, d_ff_1_q, d_ff_1_qn, not_1_out;
  wire [2:0] bit_extender_2_out;
  wire [31:0] adder_1_out, bit_extender_1_out, bit_extender_3_out, register_1_q;

  assign bit_extender_1_out = {{24{1'b0}}, in_1[7:0]};  // Bit_Extender bit_extender_1
  and and_1 (and_1_out, d_ff_1_qn, in_1[11]);
  Adder #(.width(32)) adder_1 (.a(in_2), .b(bit_extender_1_out), .out(adder_1_out));  // open: cin, cout
  D_Flip_Flop d_ff_1 (.D(and_1_out), .clk(in_4), .Q(d_ff_1_q), .Qn(d_ff_1_qn), .reset(in_5));  // open: preset
  Register #(.width(32)) register_1 (.D(adder_1_out), .en(in_3), .clk(in_4), .Q(register_1_q), .clr(in_5));
  not not_1 (not_1_out, in_1[11]);
  assign bit_extender_2_out = {{2{in_3}}, in_3};  // Bit_Extender bit_extender_2
  assign bit_extender_3_out = {{31{in_3}}, in_3};  // Bit_Extender bit_extender_3
  and and_2 (out_7, not_1_out, in_3);
  and and_3 (out_8, in_1[11], in_3);
  assign out_9 = in_1[10:8] & bit_extender_2_out;  // AND_Gate and_4, 3 bits wide
  assign out_11 = register_1_q & bit_extender_3_out;  // AND_Gate and_5, 32 bits wide
  and and_6 (out_12, d_ff_1_q, in_3);

  assign out_6 = in_1[7:0];
  assign out_10 = out_9;

  // Other names for the same wires on the sheet: Clk = in_4; E = in_3; Imm[7:0] = in_1[7:0]; R[2:0] = in_1[10:8];
  //   a = in_1[11]; Reset = in_5

  // Notes on the sheet:
  //   Delay load and hold PC for 1 cycle for the RAM to send out requested data 
endmodule
