// Logisim project ALU.circ as structural Verilog: 4 circuits, main circuit Overflow_Additionneur
module ALU (
  input  [31:0] A,
  input  [31:0] B,
  input  CarryIn,
  input  [4:0] Shift,
  input  [3:0] Codop,
  output [3:0] Flags,
  output [31:0] S
);

  wire adder_1_cout, bitselector_1_out, bitselector_2_out, CMN_C, CMP_C, overflow_additionneur_1_overflow,
       overflow_additionneur_2_overflow, overflow_soustracteur_1_overflow, overflow_soustracteur_2_overflow,
       sbc_intern_1_carry_out;
  wire [4:0] subtractor_3_out, subtractor_4_out;
  wire [31:0] ADC, and_1_out, and_2_out, and_3_out, CMN, CMP, multiplexer_3_out, multiplier_1_out, not_1_out,
       not_2_out, or_1_out, SBC, shifter_1_out, shifter_2_out, shifter_3_out, shifter_4_out,
       subtractor_1_out, xor_1_out;

  assign not_1_out = ~A;  // NOT_Gate not_1, 32 bits wide
  assign and_1_out = A & B;  // AND_Gate and_1, 32 bits wide
  assign xor_1_out = A ^ B;  // XOR_Gate xor_1, 32 bits wide
  Shifter #(.width(32)) shifter_1 (.in(B), .\dist (Shift), .out(shifter_1_out));
  Shifter #(.width(32), .shift("lr")) shifter_2 (.in(B), .\dist (Shift), .out(shifter_2_out));
  Shifter #(.width(32), .shift("ar")) shifter_3 (.in(B), .\dist (Shift), .out(shifter_3_out));
  Adder #(.width(32)) adder_1 (.a(A), .b(B), .out(ADC), .cin(CarryIn), .cout(adder_1_cout));
  Shifter #(.width(32), .shift("rr")) shifter_4 (.in(B), .\dist (Shift), .out(shifter_4_out));
  assign and_2_out = A & B;  // AND_Gate and_2, 32 bits wide
  Subtractor #(.width(32)) subtractor_1 (.a({32{1'b0}}), .b(A), .out(subtractor_1_out));  // open: bin, bout
  Subtractor #(.width(32)) subtractor_2 (.a(B), .b(A), .out(CMP), .bout(CMP_C));  // open: bin
  Adder #(.width(32)) adder_2 (.a(A), .b(B), .out(CMN), .cout(CMN_C));  // open: cin
  assign or_1_out = A | B;  // OR_Gate or_1, 32 bits wide
  Multiplier #(.width(32)) multiplier_1 (.a(A), .b(B), .out(multiplier_1_out));  // open: cin, cout
  assign and_3_out = B & not_1_out;  // AND_Gate and_3, 32 bits wide
  assign not_2_out = ~B;  // NOT_Gate not_2, 32 bits wide
  SBC_INTERN sbc_intern_1 (.Carry_in(CarryIn), .B(B), .A(A), .S(SBC), .Carry_out(sbc_intern_1_carry_out));
  Multiplexer #(.select(4), .width(32), .enable("false")) multiplexer_1 (
    .in0(and_1_out), .in1(xor_1_out), .in2(shifter_1_out), .in3(shifter_2_out), .in4(shifter_3_out),
    .in5(ADC), .in6(SBC), .in7(shifter_4_out), .in8(B), .in9(subtractor_1_out), .in10(B), .in11(B),
    .in12(or_1_out), .in13(multiplier_1_out), .in14(and_3_out), .in15(not_2_out), .out(S), .sel(Codop));
  Subtractor #(.width(5)) subtractor_3 (.a(Shift), .b(5'b00001), .out(subtractor_3_out));  // open: bin, bout
  BitSelector #(.width(32)) bitselector_1 (.in(B), .out(bitselector_1_out), .sel(subtractor_3_out));
  Subtractor #(.width(5)) subtractor_4 (.a({5{1'b0}}), .b(Shift), .out(subtractor_4_out));  // open: bin, bout
  BitSelector #(.width(32)) bitselector_2 (.in(B), .out(bitselector_2_out), .sel(subtractor_4_out));
  Multiplexer #(.select(4), .enable("false")) multiplexer_2 (
    .in0(1'b0), .in1(1'b0), .in2(bitselector_2_out), .in3(bitselector_1_out), .in4(bitselector_1_out),
    .in5(adder_1_cout), .in6(sbc_intern_1_carry_out), .in7(Flags[3]), .in8(1'b0), .in9(1'b0), .in10(CMP_C),
    .in11(CMN_C), .in12(1'b0), .in13(1'b0), .in14(1'b0), .in15(1'b0), .out(Flags[1]), .sel(Codop));
  Multiplexer #(.select(4), .width(32), .enable("false")) multiplexer_3 (
    .in0(and_1_out), .in1(xor_1_out), .in2(shifter_1_out), .in3(shifter_2_out), .in4(shifter_3_out),
    .in5(ADC), .in6(SBC), .in7(shifter_4_out), .in8(and_2_out), .in9(subtractor_1_out), .in10(CMP),
    .in11(CMN), .in12(or_1_out), .in13(multiplier_1_out), .in14(and_3_out), .in15(not_2_out),
    .out(multiplexer_3_out), .sel(Codop));
  Overflow_Additionneur overflow_additionneur_1 (.S(ADC), .A(A), .B(B), .Overflow(overflow_additionneur_1_overflow));
  Overflow_Soustracteur overflow_soustracteur_1 (.S(SBC), .A(A), .B(B), .Overflow(overflow_soustracteur_1_overflow));
  Overflow_Soustracteur overflow_soustracteur_2 (.S(CMP), .A(A), .B(B), .Overflow(overflow_soustracteur_2_overflow));
  Overflow_Additionneur overflow_additionneur_2 (.S(CMN), .A(A), .B(B), .Overflow(overflow_additionneur_2_overflow));
  Comparator #(.width(32)) comparator_1 (
    .a(multiplexer_3_out), .b({32{1'b0}}), .eq(Flags[2]), .lt(Flags[3]));  // open: gt
  Multiplexer #(.select(4), .enable("false")) multiplexer_4 (
    .in0(1'b0), .in1(1'b0), .in2(1'b0), .in3(1'b0), .in4(1'b0), .in5(overflow_additionneur_1_overflow),
    .in6(overflow_soustracteur_1_overflow), .in7(1'b0), .in8(1'b0), .in9(1'b0),
    .in10(overflow_soustracteur_2_overflow), .in11(overflow_additionneur_2_overflow), .in12(1'b0),
    .in13(1'b0), .in14(1'b0), .in15(1'b0), .out(Flags[0]), .sel(Codop));

  // Other names for the same wires on the sheet: cdp[3:0] = Codop; cri = CarryIn; V = Flags[0]; C = Flags[1];
  //   Z = Flags[2]; N = Flags[3]; sft[4:0] = Shift

  // Notes on the sheet:
  //   TST
  //   RSB
  //   CMP
  //   CMN
  //   For ROR, C = N
  //   LSL
  //   TST,CMP,CMN mettent uniquement à jour les flags, sortie = B
  //   Quand les mise a jour de Flags ne sont pas indiqué dans la DOC, nous les supposons à 0
endmodule

module Overflow_Additionneur (
  input  [31:0] S,
  input  [31:0] A,
  input  [31:0] B,
  output Overflow
);

  wire and_1_out, and_2_out, bitselector_1_out, bitselector_2_out, bitselector_3_out;

  BitSelector #(.width(32)) bitselector_1 (.in(S), .out(bitselector_1_out), .sel({5{1'b1}}));
  BitSelector #(.width(32)) bitselector_2 (.in(A), .out(bitselector_2_out), .sel({5{1'b1}}));
  BitSelector #(.width(32)) bitselector_3 (.in(B), .out(bitselector_3_out), .sel({5{1'b1}}));
  and and_1 (and_1_out, ~bitselector_1_out, bitselector_2_out, bitselector_3_out);  // AND_Gate
  and and_2 (and_2_out, bitselector_1_out, ~bitselector_2_out, ~bitselector_3_out);  // AND_Gate
  or or_1 (Overflow, and_1_out, and_2_out);
endmodule

module Overflow_Soustracteur (
  input  [31:0] S,
  input  [31:0] A,
  input  [31:0] B,
  output Overflow
);

  wire and_1_out, and_2_out, bitselector_1_out, bitselector_2_out, bitselector_3_out;

  BitSelector #(.width(32)) bitselector_1 (.in(S), .out(bitselector_1_out), .sel({5{1'b1}}));
  BitSelector #(.width(32)) bitselector_2 (.in(A), .out(bitselector_2_out), .sel({5{1'b1}}));
  BitSelector #(.width(32)) bitselector_3 (.in(B), .out(bitselector_3_out), .sel({5{1'b1}}));
  and and_1 (and_1_out, bitselector_1_out, ~bitselector_2_out, bitselector_3_out);  // AND_Gate
  and and_2 (and_2_out, ~bitselector_1_out, bitselector_2_out, ~bitselector_3_out);  // AND_Gate
  or or_1 (Overflow, and_1_out, and_2_out);
endmodule

module SBC_INTERN (
  input  Carry_in,
  input  [31:0] B,
  input  [31:0] A,
  output [31:0] S,
  output Carry_out
);

  wire not_1_out;
  wire [31:0] adder_1_out, negator_1_out, negator_2_out;

  not not_1 (not_1_out, Carry_in);
  Negator #(.width(32)) negator_1 (.in(A), .out(negator_1_out));
  Negator #(.width(32)) negator_2 (.in(32'h1), .out(negator_2_out));
  Adder #(.width(32)) adder_1 (.a(B), .b(negator_1_out), .out(adder_1_out), .cin(not_1_out));  // open: cout
  Adder #(.width(32)) adder_2 (.a(adder_1_out), .b(negator_2_out), .out(S), .cout(Carry_out));  // open: cin

  // Notes on the sheet:
  //   La retenue entrante doit etre inversé
endmodule
